# Fritzing sketch nextbus (saved by Fritzing 0.8.7b)
breadboards: 1

parts:
  Arduino = Arduino Mega 2560 (Rev3)
  CC1 = Adafruit CC3000 Shield for Arduino
  BATT1 = LiPoly Battery (1300mAh)
  D1 = SOLAR-IXYS [package=solarbit-12x1]
  CHARGER1 = USB_LiIon_LiPoly_Charger_v1.2

nets:
  Panel Temperature: Arduino.A0
  N1: Arduino.D18/TX1, CC1.IRQ
  GND/Panel GND/Panel On: Arduino.GND, CHARGER1.load_minus_1
  Panel Border_CONTROL: Arduino.D9_PWM
  Panel DISCHARGE: Arduino.D8_PWM
  Panel VTCON: Arduino.3V3
  N2: Arduino.VIN, CHARGER1.load_plus_1
  Serial RX: Arduino.D0_RX0
  Serial TX: Arduino.D1_TX0
  PANEL ~EPD_CS: Arduino.D2_PWM
  Panel RST/SBTDIO: Arduino.D3_PWM
  Panel TEST/SBWTCK: Arduino.D4_PWM
  Panel PWM: Arduino.D5_PWM
  Panel ~RESET: Arduino.D6_PWM
  Panel BUSY: Arduino.D7_PWM
  N3: Arduino.D35, CC1.CCS
  N4: Arduino.D36, CC1.WEN
  N5: Arduino.D37, CC1.WCS
  Panel SPI_MOSI: Arduino.D50, CC1.MOSI
  Panel SPI_MISO: Arduino.D51, CC1.MISO
  Panel SPI_CLK: Arduino.D52, CC1.CLK
  VCC3V: CC1.3V
  N6: BATT1.positive, CHARGER1.batt_plus_1
  N7: BATT1.negative, CHARGER1.batt_minus_1
  N8: D1.A, CHARGER1.dcin_minus_1
  N9: D1.C, CHARGER1.dcin_plus_1

custom parts:
  LiPoly Battery (1300mAh): Lithium Ion Polymer Battery (1300mAh)
